# Fritzing sketch 202012_tac_shield_v2.0.2_03 (saved by Fritzing 0.9.3b)
circuit board: 6.88566cm x 5.36311cm
breadboards: 1

parts:
  JP1 = Header 4 [part_number="gas sensor" package=molex-1x4_lock]
  JP9 = Header 4 [part_number=i2c package=molex-1x4_lock]
  JP3 = Header 3 [part_number=pH package=molex-1x3_lock]
  JP2 = Header 3 [part_number=LED package=molex-1x3_lock]
  JP8 = Header 6 [part_number=spi package=molex-1x6_lock]
  PCB1 = Arduino Shield PCB  # not connected
  JP4 = Header 3 [part_number=humidity package=molex-1x3_lock]
  JP5 = Header 3 [part_number=temp package=molex-1x3_lock]
  R3 = Resistor [tolerance=±5% resistance=4.7k package=THT]
  JP6 = Header 3 [part_number=fishtank package=molex-1x3_lock]
  JP7 = Header 3 [part_number=moisture package=molex-1x3_lock]
  arduino = Arduino Uno (Rev3)

nets:
  GND: JP1.1, JP9.1, JP3.1, JP2.1, JP8.1, JP4.1, JP5.1, JP6.1, JP7.1, arduino.GND
  N1: JP1.2, JP9.2, JP3.2, JP2.2, JP8.2, JP4.2, JP5.2, R3.Pin_0, JP6.2, JP7.2, arduino.5V
  N2: JP1.3, JP9.3, arduino.A5/SCL
  N3: JP1.4, JP9.4, arduino.A4/SDA
  N4: JP3.3, arduino.A2
  N5: JP2.3, arduino.D6_PWM
  N6: JP8.3, arduino.D10_PWM/SS
  N7: JP8.4, arduino.D11_PWM/MOSI
  N8: JP8.5, arduino.D12/MISO
  N9: JP8.6, arduino.D13/SCK
  N10: JP4.3, arduino.D4
  N11: JP5.3, R3.Pin_1, arduino.D3_PWM
  N12: JP6.3, arduino.D9_PWM
  N13: JP7.3, arduino.A3

notes:
  teleagriculture v2.0.2
  sck
  miso
  mosi
  ss
  5v
  gnd
  sda
  scl
  s
  +
  -

custom parts:
  Arduino Shield PCB: Plain PCB Shaped to fit an Arduino "Shield"
